# Fritzing sketch piezo piano (saved by Fritzing 0.9.3b)
breadboards: 1

parts:
  R1 = Photocell (LDR) [package=THT]
  R2 = Photocell (LDR) [package=THT]
  R4 = Photocell (LDR) [package=THT]
  R5 = Resistor [tolerance=±5% resistance=1k package=THT]
  R8 = Photocell (LDR) [package=THT]
  R10 = Resistor [tolerance=±5% resistance=1k package=THT]
  R11 = Resistor [tolerance=±5% resistance=1k package=THT]
  R12 = Resistor [tolerance=±5% resistance=1k package=THT]
  J1 = Piezo Speaker

nets:
  N1: R1.pin_1, R5.Pin_0
  N2: R2.pin_1, R11.Pin_0
  N3: R4.pin_1, R10.Pin_0
  N4: R5.Pin_1, J1.pin1
  N5: R8.pin_1, R12.Pin_0

notes:
  3.3V
  P6.1
  P6.2
  P6.3
  P6.4
  GND
  P2.3
